// Logisim project practica.circ as structural Verilog: 13 circuits, main circuit main
module main (
  input  [7:0] I0,
  input  [7:0] I1,
  input  [7:0] I2,
  input  [7:0] I3,
  input  [7:0] I4,
  input  [7:0] I5,
  input  [7:0] I6,
  input  [7:0] I7,
  output [7:0] S0,
  output [7:0] S1,
  output [7:0] S2,
  output [7:0] S3,
  output [7:0] S4,
  output [7:0] S5,
  output [7:0] S6,
  output [7:0] S7
);

  // Probe on I0
  // Probe on I1
  // Probe on I2
  // Probe on I3
  // Probe on I4
  // Probe on I5
  // Probe on I6
  // Probe on I7
  order_8 order_8_1 (
    .A(I0), .B(I1), .C(I2), .D(I3), .E(I4), .F(I5), .G(I6), .H(I7), .As(S0), .Bs(S1), .Cs(S2), .Ds(S3),
    .Es(S4), .Fs(S5), .Gs(S6), .Hs(S7));
  // Probe on S0
  // Probe on S1
  // Probe on S2
  // Probe on S3
  // Probe on S4
  // Probe on S5
  // Probe on S6
  // Probe on S7
endmodule

module one_bit_component (
  input  A,
  input  B,
  input  C1,
  input  C2,
  output C1o,
  output C2o
);

  wire and_1_out, and_2_out, and_3_out, and_4_out, and_5_out, and_6_out, not_1_out, not_2_out;

  not not_1 (not_1_out, A);
  not not_2 (not_2_out, B);
  and and_1 (and_1_out, not_2_out, A);
  and and_2 (and_2_out, A, C1);
  and and_3 (and_3_out, not_2_out, C1);
  and and_4 (and_4_out, not_1_out, B);
  and and_5 (and_5_out, not_1_out, C2);
  and and_6 (and_6_out, B, C2);
  or or_1 (C1o, and_1_out, and_2_out, and_3_out);
  or or_2 (C2o, and_4_out, and_5_out, and_6_out);
endmodule

module eight_bit_component (
  input  [7:0] A,
  input  [7:0] B,
  output C1,
  output C2
);

  wire one_bit_component_1_c1o, one_bit_component_1_c2o, one_bit_component_2_c1o, one_bit_component_2_c2o,
       one_bit_component_3_c1o, one_bit_component_3_c2o, one_bit_component_4_c1o, one_bit_component_4_c2o,
       one_bit_component_5_c1o, one_bit_component_5_c2o, one_bit_component_6_c1o, one_bit_component_6_c2o,
       one_bit_component_7_c1o, one_bit_component_7_c2o;

  one_bit_component one_bit_component_1 (
    .A(A[0]), .B(B[0]), .C1(1'b0), .C2(1'b0), .C1o(one_bit_component_1_c1o), .C2o(one_bit_component_1_c2o));
  one_bit_component one_bit_component_2 (
    .A(A[1]), .B(B[1]), .C1(one_bit_component_1_c1o), .C2(one_bit_component_1_c2o),
    .C1o(one_bit_component_2_c1o), .C2o(one_bit_component_2_c2o));
  one_bit_component one_bit_component_3 (
    .A(A[2]), .B(B[2]), .C1(one_bit_component_2_c1o), .C2(one_bit_component_2_c2o),
    .C1o(one_bit_component_3_c1o), .C2o(one_bit_component_3_c2o));
  one_bit_component one_bit_component_4 (
    .A(A[3]), .B(B[3]), .C1(one_bit_component_3_c1o), .C2(one_bit_component_3_c2o),
    .C1o(one_bit_component_4_c1o), .C2o(one_bit_component_4_c2o));
  one_bit_component one_bit_component_5 (
    .A(A[4]), .B(B[4]), .C1(one_bit_component_4_c1o), .C2(one_bit_component_4_c2o),
    .C1o(one_bit_component_5_c1o), .C2o(one_bit_component_5_c2o));
  one_bit_component one_bit_component_6 (
    .A(A[5]), .B(B[5]), .C1(one_bit_component_5_c1o), .C2(one_bit_component_5_c2o),
    .C1o(one_bit_component_6_c1o), .C2o(one_bit_component_6_c2o));
  one_bit_component one_bit_component_7 (
    .A(A[6]), .B(B[6]), .C1(one_bit_component_6_c1o), .C2(one_bit_component_6_c2o),
    .C1o(one_bit_component_7_c1o), .C2o(one_bit_component_7_c2o));
  one_bit_component one_bit_component_8 (
    .A(B[7]), .B(A[7]), .C1(one_bit_component_7_c1o), .C2(one_bit_component_7_c2o), .C1o(C1), .C2o(C2));
endmodule

module comp2_2 (
  input  A,
  input  B,
  input  C1o,
  output LD,
  output GD
);

  wire and_1_out, and_2_out, and_3_out, and_4_out, not_1_out;

  not not_1 (not_1_out, C1o);
  and and_1 (and_1_out, A, not_1_out);
  and and_2 (and_2_out, B, C1o);
  and and_3 (and_3_out, B, not_1_out);
  and and_4 (and_4_out, A, C1o);
  or or_1 (LD, and_1_out, and_2_out);
  or or_2 (GD, and_3_out, and_4_out);
endmodule

module comp4_2 (
  input  [3:0] A,
  input  [3:0] B,
  input  C,
  output [3:0] less,
  output [3:0] greater
);

  comp2_2 comp2_2_1 (.A(A[0]), .B(B[0]), .C1o(C), .LD(less[0]), .GD(greater[0]));
  comp2_2 comp2_2_2 (.A(A[1]), .B(B[1]), .C1o(C), .LD(less[1]), .GD(greater[1]));
  comp2_2 comp2_2_3 (.A(A[2]), .B(B[2]), .C1o(C), .LD(less[2]), .GD(greater[2]));
  comp2_2 comp2_2_4 (.A(A[3]), .B(B[3]), .C1o(C), .LD(less[3]), .GD(greater[3]));
endmodule

module comp8_2 (
  input  [7:0] A,
  input  [7:0] B,
  input  C,
  output [7:0] less,
  output [7:0] greater
);

  comp4_2 comp4_2_1 (.A(A[3:0]), .B(B[3:0]), .C(C), .less(less[3:0]), .greater(greater[3:0]));
  comp4_2 comp4_2_2 (.A(A[7:4]), .B(B[7:4]), .C(C), .less(less[7:4]), .greater(greater[7:4]));
endmodule

module order_4 (
  input  [7:0] A,
  input  [7:0] B,
  input  [7:0] C,
  input  [7:0] D,
  output [7:0] As,
  output [7:0] Bs,
  output [7:0] Cs,
  output [7:0] Ds
);

  wire [7:0] switch_1_higher, switch_1_less, switch_2_higher, switch_2_less, switch_3_higher, switch_4_less;

  switch switch_1 (.A(A), .B(C), .less(switch_1_less), .higher(switch_1_higher));
  switch switch_2 (.A(B), .B(D), .less(switch_2_less), .higher(switch_2_higher));
  switch switch_3 (.A(switch_1_less), .B(switch_2_less), .less(As), .higher(switch_3_higher));
  switch switch_4 (.A(switch_1_higher), .B(switch_2_higher), .less(switch_4_less), .higher(Ds));
  switch switch_5 (.A(switch_3_higher), .B(switch_4_less), .less(Bs), .higher(Cs));
endmodule

module switch (
  input  [7:0] A,
  input  [7:0] B,
  output [7:0] less,
  output [7:0] higher
);

  wire eight_bit_component_1_c1;

  eight_bit_component eight_bit_component_1 (.A(A), .B(B), .C1(eight_bit_component_1_c1));  // open: C2
  comp8_2 comp8_2_1 (.A(A), .B(B), .C(eight_bit_component_1_c1), .less(less), .greater(higher));
endmodule

module order_5 (
  input  [7:0] A,
  input  [7:0] B,
  input  [7:0] C,
  input  [7:0] D,
  input  [7:0] E,
  output [7:0] As,
  output [7:0] Bs,
  output [7:0] Cs,
  output [7:0] Ds,
  output [7:0] Es
);

  wire [7:0] order_4_1_as, order_4_1_bs, order_4_1_cs, order_4_1_ds, switch_1_less, switch_2_less,
       switch_3_less;

  order_4 order_4_1 (
    .A(A), .B(B), .C(C), .D(D), .As(order_4_1_as), .Bs(order_4_1_bs), .Cs(order_4_1_cs), .Ds(order_4_1_ds));
  switch switch_1 (.A(order_4_1_ds), .B(E), .less(switch_1_less), .higher(Es));
  switch switch_2 (.A(order_4_1_cs), .B(switch_1_less), .less(switch_2_less), .higher(Ds));
  switch switch_3 (.A(order_4_1_bs), .B(switch_2_less), .less(switch_3_less), .higher(Cs));
  switch switch_4 (.A(order_4_1_as), .B(switch_3_less), .less(As), .higher(Bs));
endmodule

module order_6 (
  input  [7:0] A,
  input  [7:0] B,
  input  [7:0] C,
  input  [7:0] D,
  input  [7:0] E,
  input  [7:0] F,
  output [7:0] As,
  output [7:0] Bs,
  output [7:0] Cs,
  output [7:0] Ds,
  output [7:0] Es,
  output [7:0] Fs
);

  wire [7:0] order_5_1_as, order_5_1_bs, order_5_1_cs, order_5_1_ds, order_5_1_es, switch_1_less,
       switch_2_less, switch_3_less, switch_4_less;

  order_5 order_5_1 (
    .A(A), .B(B), .C(C), .D(D), .E(E), .As(order_5_1_as), .Bs(order_5_1_bs), .Cs(order_5_1_cs),
    .Ds(order_5_1_ds), .Es(order_5_1_es));
  switch switch_1 (.A(order_5_1_es), .B(F), .less(switch_1_less), .higher(Fs));
  switch switch_2 (.A(order_5_1_ds), .B(switch_1_less), .less(switch_2_less), .higher(Es));
  switch switch_3 (.A(order_5_1_cs), .B(switch_2_less), .less(switch_3_less), .higher(Ds));
  switch switch_4 (.A(order_5_1_bs), .B(switch_3_less), .less(switch_4_less), .higher(Cs));
  switch switch_5 (.A(order_5_1_as), .B(switch_4_less), .less(As), .higher(Bs));
endmodule

module order_7 (
  input  [7:0] A,
  input  [7:0] B,
  input  [7:0] C,
  input  [7:0] D,
  input  [7:0] E,
  input  [7:0] F,
  input  [7:0] G,
  output [7:0] As,
  output [7:0] Bs,
  output [7:0] Cs,
  output [7:0] Ds,
  output [7:0] Es,
  output [7:0] Fs,
  output [7:0] Gs
);

  wire [7:0] order_6_1_as, order_6_1_bs, order_6_1_cs, order_6_1_ds, order_6_1_es, order_6_1_fs,
       switch_1_less, switch_2_less, switch_3_less, switch_4_less, switch_5_less;

  switch switch_1 (.A(order_6_1_fs), .B(G), .less(switch_1_less), .higher(Gs));
  order_6 order_6_1 (
    .A(A), .B(B), .C(C), .D(D), .E(E), .F(F), .As(order_6_1_as), .Bs(order_6_1_bs), .Cs(order_6_1_cs),
    .Ds(order_6_1_ds), .Es(order_6_1_es), .Fs(order_6_1_fs));
  switch switch_2 (.A(order_6_1_es), .B(switch_1_less), .less(switch_2_less), .higher(Fs));
  switch switch_3 (.A(order_6_1_ds), .B(switch_2_less), .less(switch_3_less), .higher(Es));
  switch switch_4 (.A(order_6_1_cs), .B(switch_3_less), .less(switch_4_less), .higher(Ds));
  switch switch_5 (.A(order_6_1_bs), .B(switch_4_less), .less(switch_5_less), .higher(Cs));
  switch switch_6 (.A(order_6_1_as), .B(switch_5_less), .less(As), .higher(Bs));
endmodule

module order_8_2 (
  input  [7:0] A,
  input  [7:0] B,
  input  [7:0] C,
  input  [7:0] D,
  input  [7:0] E,
  input  [7:0] F,
  input  [7:0] G,
  input  [7:0] H,
  output [7:0] As,
  output [7:0] Bs,
  output [7:0] Cs,
  output [7:0] Ds,
  output [7:0] Es,
  output [7:0] Fs,
  output [7:0] Gs,
  output [7:0] Hs
);

  wire [7:0] order_7_1_as, order_7_1_bs, order_7_1_cs, order_7_1_ds, order_7_1_es, order_7_1_fs,
       order_7_1_gs, switch_1_less, switch_2_less, switch_3_less, switch_4_less, switch_5_less, switch_6_less;

  switch switch_1 (.A(order_7_1_gs), .B(H), .less(switch_1_less), .higher(Hs));
  order_7 order_7_1 (
    .A(A), .B(B), .C(C), .D(D), .E(E), .F(F), .G(G), .As(order_7_1_as), .Bs(order_7_1_bs), .Cs(order_7_1_cs),
    .Ds(order_7_1_ds), .Es(order_7_1_es), .Fs(order_7_1_fs), .Gs(order_7_1_gs));
  switch switch_2 (.A(order_7_1_fs), .B(switch_1_less), .less(switch_2_less), .higher(Gs));
  switch switch_3 (.A(order_7_1_es), .B(switch_2_less), .less(switch_3_less), .higher(Fs));
  switch switch_4 (.A(order_7_1_ds), .B(switch_3_less), .less(switch_4_less), .higher(Es));
  switch switch_5 (.A(order_7_1_cs), .B(switch_4_less), .less(switch_5_less), .higher(Ds));
  switch switch_6 (.A(order_7_1_bs), .B(switch_5_less), .less(switch_6_less), .higher(Cs));
  switch switch_7 (.A(order_7_1_as), .B(switch_6_less), .less(As), .higher(Bs));
endmodule

module order_8 (
  input  [7:0] A,
  input  [7:0] B,
  input  [7:0] C,
  input  [7:0] D,
  input  [7:0] E,
  input  [7:0] F,
  input  [7:0] G,
  input  [7:0] H,
  output [7:0] As,
  output [7:0] Bs,
  output [7:0] Cs,
  output [7:0] Ds,
  output [7:0] Es,
  output [7:0] Fs,
  output [7:0] Gs,
  output [7:0] Hs
);

  wire [7:0] order_4_1_as, order_4_1_bs, order_4_1_cs, order_4_1_ds, order_4_2_as, order_4_2_bs,
       order_4_2_cs, order_4_2_ds, order_4_3_cs, order_4_3_ds, order_4_4_as, order_4_4_bs;

  order_4 order_4_1 (
    .A(A), .B(B), .C(E), .D(F), .As(order_4_1_as), .Bs(order_4_1_bs), .Cs(order_4_1_cs), .Ds(order_4_1_ds));
  order_4 order_4_2 (
    .A(C), .B(D), .C(G), .D(H), .As(order_4_2_as), .Bs(order_4_2_bs), .Cs(order_4_2_cs), .Ds(order_4_2_ds));
  order_4 order_4_3 (
    .A(order_4_1_as), .B(order_4_1_bs), .C(order_4_2_as), .D(order_4_2_bs), .As(As), .Bs(Bs),
    .Cs(order_4_3_cs), .Ds(order_4_3_ds));
  order_4 order_4_4 (
    .A(order_4_1_cs), .B(order_4_1_ds), .C(order_4_2_cs), .D(order_4_2_ds), .As(order_4_4_as),
    .Bs(order_4_4_bs), .Cs(Gs), .Ds(Hs));
  order_4 order_4_5 (
    .A(order_4_3_cs), .B(order_4_3_ds), .C(order_4_4_as), .D(order_4_4_bs), .As(Cs), .Bs(Ds), .Cs(Es), .Ds(Fs));
endmodule
