// Logisim project speed_control.circ as structural Verilog: 10 circuits, main circuit main
module main (
  output [2:0] CS,
  output [2:0] NS,
  output [1:0] out_3,
  output [1:0] out_4,
  output [1:0] out_5,
  output [1:0] out_6
);

  wire clock_1_out, D_out, e2bit_to3bit_1_n0, e2bit_to3bit_1_n1, e2bit_to3bit_1_n2, la2bit_to3bit_1_n0,
       la2bit_to3bit_1_n1, la2bit_to3bit_1_n2, n3bit_to7seg_1_a, n3bit_to7seg_1_b, n3bit_to7seg_1_c,
       n3bit_to7seg_1_d, n3bit_to7seg_1_e, n3bit_to7seg_1_f, n3bit_to7seg_1_g, ra2bit_to3bit_1_n0,
       ra2bit_to3bit_1_n1, ra2bit_to3bit_1_n2, t2bit_to3bit_1_n0, t2bit_to3bit_1_n1, t2bit_to3bit_1_n2, U_out;
  wire [3:0] n3bit_to20seg_1_row0, n3bit_to20seg_1_row1, n3bit_to20seg_1_row2, n3bit_to20seg_1_row3,
       n3bit_to20seg_1_row4, n3bit_to20seg_2_row0, n3bit_to20seg_2_row1, n3bit_to20seg_2_row2,
       n3bit_to20seg_2_row3, n3bit_to20seg_2_row4, n3bit_to20seg_3_row0, n3bit_to20seg_3_row1,
       n3bit_to20seg_3_row2, n3bit_to20seg_3_row3, n3bit_to20seg_3_row4, n3bit_to20seg_4_row0,
       n3bit_to20seg_4_row1, n3bit_to20seg_4_row2, n3bit_to20seg_4_row3, n3bit_to20seg_4_row4;

  Button U (.out(U_out));
  Button D (.out(D_out));
  Joystick #(.bits(2)) joystick_1 (.x(out_3), .y(out_4));
  Joystick #(.bits(2)) joystick_2 (.x(out_5), .y(out_6));
  speed_control speed_control_1 (
    .CS2(CS[2]), .CS1(CS[1]), .CS0(CS[0]), .U(U_out), .D(D_out), .NS2(NS[2]), .NS1(NS[1]), .NS0(NS[0]));
  Register #(.width(3)) register_1 (.D(NS), .Q(CS), .clk(clock_1_out));  // open: en, clr
  Clock clock_1 (.out(clock_1_out));
  T2bit_to3bit t2bit_to3bit_1 (
    .D1(out_3[1]), .D0(out_3[0]), .N2(t2bit_to3bit_1_n2), .N1(t2bit_to3bit_1_n1), .N0(t2bit_to3bit_1_n0));
  E2bit_to3bit e2bit_to3bit_1 (
    .D1(out_4[1]), .D0(out_4[0]), .N2(e2bit_to3bit_1_n2), .N1(e2bit_to3bit_1_n1), .N0(e2bit_to3bit_1_n0));
  LA2bit_to3bit la2bit_to3bit_1 (
    .D1(out_5[1]), .D0(out_5[0]), .N2(la2bit_to3bit_1_n2), .N1(la2bit_to3bit_1_n1), .N0(la2bit_to3bit_1_n0));
  RA2bit_to3bit ra2bit_to3bit_1 (
    .D1(out_5[1]), .D0(out_5[0]), .N2(ra2bit_to3bit_1_n2), .N1(ra2bit_to3bit_1_n1), .N0(ra2bit_to3bit_1_n0));
  _3bit_to7seg u_3bit_to7seg_1 (
    .D2(CS[2]), .D1(CS[1]), .D0(CS[0]), .a(n3bit_to7seg_1_a), .b(n3bit_to7seg_1_b), .c(n3bit_to7seg_1_c),
    .d(n3bit_to7seg_1_d), .e(n3bit_to7seg_1_e), .f(n3bit_to7seg_1_f), .g(n3bit_to7seg_1_g));
  _3bit_to20seg u_3bit_to20seg_1 (
    .N2(t2bit_to3bit_1_n2), .N1(t2bit_to3bit_1_n1), .N0(t2bit_to3bit_1_n0), .Row0(n3bit_to20seg_1_row0),
    .Row1(n3bit_to20seg_1_row1), .Row2(n3bit_to20seg_1_row2), .Row3(n3bit_to20seg_1_row3),
    .Row4(n3bit_to20seg_1_row4));
  _3bit_to20seg u_3bit_to20seg_2 (
    .N2(e2bit_to3bit_1_n2), .N1(e2bit_to3bit_1_n1), .N0(e2bit_to3bit_1_n0), .Row0(n3bit_to20seg_2_row0),
    .Row1(n3bit_to20seg_2_row1), .Row2(n3bit_to20seg_2_row2), .Row3(n3bit_to20seg_2_row3),
    .Row4(n3bit_to20seg_2_row4));
  _3bit_to20seg u_3bit_to20seg_3 (
    .N2(la2bit_to3bit_1_n2), .N1(la2bit_to3bit_1_n1), .N0(la2bit_to3bit_1_n0), .Row0(n3bit_to20seg_3_row0),
    .Row1(n3bit_to20seg_3_row1), .Row2(n3bit_to20seg_3_row2), .Row3(n3bit_to20seg_3_row3),
    .Row4(n3bit_to20seg_3_row4));
  _3bit_to20seg u_3bit_to20seg_4 (
    .N2(ra2bit_to3bit_1_n2), .N1(ra2bit_to3bit_1_n1), .N0(ra2bit_to3bit_1_n0), .Row0(n3bit_to20seg_4_row0),
    .Row1(n3bit_to20seg_4_row1), .Row2(n3bit_to20seg_4_row2), .Row3(n3bit_to20seg_4_row3),
    .Row4(n3bit_to20seg_4_row4));
  _7_Segment_Display u_7_segment_display_1 (
    .g(n3bit_to7seg_1_g), .f(n3bit_to7seg_1_f), .a(n3bit_to7seg_1_a), .b(n3bit_to7seg_1_b),
    .e(n3bit_to7seg_1_e), .d(n3bit_to7seg_1_d), .c(n3bit_to7seg_1_c));  // open: dp
  DotMatrix #(.inputtype("row"), .matrixcols(4), .matrixrows(5)) dotmatrix_1 (
    .row0(n3bit_to20seg_1_row0), .row1(n3bit_to20seg_1_row1), .row2(n3bit_to20seg_1_row2),
    .row3(n3bit_to20seg_1_row3), .row4(n3bit_to20seg_1_row4));
  DotMatrix #(.inputtype("row"), .matrixcols(4), .matrixrows(5)) dotmatrix_2 (
    .row0(n3bit_to20seg_2_row0), .row1(n3bit_to20seg_2_row1), .row2(n3bit_to20seg_2_row2),
    .row3(n3bit_to20seg_2_row3), .row4(n3bit_to20seg_2_row4));
  DotMatrix #(.inputtype("row"), .matrixcols(4), .matrixrows(5)) dotmatrix_3 (
    .row0(n3bit_to20seg_3_row0), .row1(n3bit_to20seg_3_row1), .row2(n3bit_to20seg_3_row2),
    .row3(n3bit_to20seg_3_row3), .row4(n3bit_to20seg_3_row4));
  DotMatrix #(.inputtype("row"), .matrixcols(4), .matrixrows(5)) dotmatrix_4 (
    .row0(n3bit_to20seg_4_row0), .row1(n3bit_to20seg_4_row1), .row2(n3bit_to20seg_4_row2),
    .row3(n3bit_to20seg_4_row3), .row4(n3bit_to20seg_4_row4));

  // Notes on the sheet:
  //   Botones
  //   Elevadores y timón
  //   Alerones
  //   Timón
  //   Elevadores
  //   Alerón izquierdo
  //   Alerón derecho
endmodule

module speed_control (
  input  CS2,
  input  CS1,
  input  CS0,
  input  U,
  input  D,
  output NS2,
  output NS1,
  output NS0
);

  wire and_1_out, and_2_out, and_3_out, and_4_out, and_5_out, and_6_out, and_7_out, and_8_out, and_9_out,
       and_10_out, and_11_out, and_12_out, and_13_out, and_14_out, and_15_out, and_16_out, and_17_out,
       not_1_out, not_2_out, not_3_out, not_4_out, not_5_out, not_6_out, not_7_out, not_8_out, not_9_out,
       not_10_out, not_11_out, not_12_out, not_13_out, not_14_out, not_15_out, not_16_out, not_17_out,
       not_18_out, not_19_out, not_20_out;

  not not_1 (not_1_out, D);
  not not_2 (not_2_out, D);
  not not_3 (not_3_out, CS1);
  not not_4 (not_4_out, D);
  not not_5 (not_5_out, CS0);
  not not_6 (not_6_out, D);
  not not_7 (not_7_out, U);
  not not_8 (not_8_out, CS1);
  not not_9 (not_9_out, CS0);
  not not_10 (not_10_out, U);
  not not_11 (not_11_out, D);
  not not_12 (not_12_out, CS0);
  not not_13 (not_13_out, D);
  not not_14 (not_14_out, U);
  not not_15 (not_15_out, D);
  not not_16 (not_16_out, CS0);
  not not_17 (not_17_out, U);
  not not_18 (not_18_out, CS0);
  not not_19 (not_19_out, U);
  not not_20 (not_20_out, D);
  and and_1 (and_1_out, CS1, CS0, U, not_1_out);
  and and_2 (and_2_out, CS2, not_2_out);
  and and_3 (and_3_out, CS2, U);
  and and_4 (and_4_out, CS2, CS0);
  and and_5 (and_5_out, CS2, CS1);
  and and_6 (and_6_out, not_3_out, CS0, U, not_4_out);
  and and_7 (and_7_out, CS1, not_5_out, not_6_out);
  and and_8 (and_8_out, CS1, U, D);
  and and_9 (and_9_out, CS1, CS0, not_7_out);
  and and_10 (and_10_out, CS2, not_8_out, not_9_out, not_10_out, D);
  and and_11 (and_11_out, CS2, CS1, not_11_out);
  and and_12 (and_12_out, not_12_out, U, not_13_out);
  and and_13 (and_13_out, CS0, not_14_out, not_15_out);
  and and_14 (and_14_out, CS0, U, D);
  and and_15 (and_15_out, CS1, not_16_out, not_17_out, D);
  and and_16 (and_16_out, CS2, not_18_out, not_19_out, D);
  and and_17 (and_17_out, CS2, CS1, CS0, not_20_out);
  or or_1 (NS2, and_1_out, and_2_out, and_3_out, and_4_out, and_5_out);
  or or_2 (NS1, and_6_out, and_7_out, and_8_out, and_9_out, and_10_out, and_11_out);
  or or_3 (NS0, and_12_out, and_13_out, and_14_out, and_15_out, and_16_out, and_17_out);
endmodule

module _3bit_to7seg (
  input  D2,
  input  D1,
  input  D0,
  output a,
  output b,
  output c,
  output d,
  output e,
  output f,
  output g
);

  wire and_1_out, and_2_out, and_3_out, and_4_out, and_5_out, and_6_out, and_7_out, and_8_out, and_9_out,
       and_10_out, and_11_out, and_12_out, and_13_out, and_14_out, and_15_out, and_16_out, not_1_out,
       not_2_out, not_3_out, not_4_out, not_5_out, not_6_out, not_7_out, not_8_out, not_9_out, not_10_out,
       not_11_out, not_12_out, not_13_out, not_14_out, not_15_out, not_16_out, not_17_out, not_18_out,
       not_19_out, not_20_out, not_21_out;

  not not_1 (not_1_out, D2);
  not not_2 (not_2_out, D0);
  not not_3 (not_3_out, D1);
  not not_4 (not_4_out, D0);
  not not_5 (not_5_out, D1);
  not not_6 (not_6_out, D2);
  not not_7 (not_7_out, D0);
  not not_8 (not_8_out, D2);
  not not_9 (not_9_out, D0);
  not not_10 (not_10_out, D1);
  not not_11 (not_11_out, D2);
  not not_12 (not_12_out, D0);
  not not_13 (not_13_out, D0);
  not not_14 (not_14_out, D1);
  not not_15 (not_15_out, D0);
  not not_16 (not_16_out, D1);
  not not_17 (not_17_out, D0);
  not not_18 (not_18_out, D2);
  not not_19 (not_19_out, D1);
  not not_20 (not_20_out, D0);
  and and_1 (and_1_out, not_1_out, not_2_out);
  and and_2 (and_2_out, D2, D0);
  not not_21 (not_21_out, D2);
  and and_3 (and_3_out, not_3_out, not_4_out);
  and and_4 (and_4_out, D1, D0);
  or or_1 (c, not_5_out, D0, D2);
  and and_5 (and_5_out, not_6_out, not_7_out);
  and and_6 (and_6_out, not_8_out, D1);
  and and_7 (and_7_out, D1, not_9_out);
  and and_8 (and_8_out, D2, not_10_out, D0);
  and and_9 (and_9_out, not_11_out, not_12_out);
  and and_10 (and_10_out, D1, not_13_out);
  and and_11 (and_11_out, not_14_out, not_15_out);
  and and_12 (and_12_out, D2, not_16_out);
  and and_13 (and_13_out, D2, not_17_out);
  and and_14 (and_14_out, not_18_out, D1);
  and and_15 (and_15_out, D2, not_19_out);
  and and_16 (and_16_out, D2, not_20_out);
  or or_2 (a, and_1_out, D1, and_2_out);
  or or_3 (b, not_21_out, and_3_out, and_4_out);
  or or_4 (d, and_5_out, and_6_out, and_7_out, and_8_out);
  or or_5 (e, and_9_out, and_10_out);
  or or_6 (f, and_11_out, and_12_out, and_13_out);
  or or_7 (g, and_14_out, and_15_out, and_16_out);
endmodule

module T2bit_to3bit (
  input  D1,
  input  D0,
  output N2,
  output N1,
  output N0
);

  wire and_1_out, and_2_out, and_3_out, and_4_out, not_1_out, not_2_out, not_4_out, not_5_out;

  not not_1 (not_1_out, D1);
  not not_2 (not_2_out, D0);
  not not_3 (N1, D0);
  not not_4 (not_4_out, D1);
  not not_5 (not_5_out, D0);
  and and_1 (and_1_out, not_1_out, not_2_out);
  and and_2 (and_2_out, D1, D0);
  and and_3 (and_3_out, not_4_out, not_5_out);
  and and_4 (and_4_out, D1, D0);
  or or_1 (N2, and_1_out, and_2_out);
  or or_2 (N0, and_3_out, and_4_out);
endmodule

module E2bit_to3bit (
  input  D1,
  input  D0,
  output N2,
  output N1,
  output N0
);

  wire and_1_out, and_2_out, not_1_out, not_2_out, not_3_out;

  not not_1 (not_1_out, D1);
  not not_2 (not_2_out, D0);
  not not_3 (not_3_out, D1);
  and and_1 (and_1_out, not_1_out, not_2_out);
  and and_2 (and_2_out, D1, D0);
  or or_1 (N0, not_3_out, D0);
  or or_2 (N2, and_1_out, and_2_out);

  assign N1 = 1'b1;
endmodule

module P2_3bit_20seg (
  input  N2,
  input  N1,
  input  N0,
  output L00,
  output L01,
  output L02,
  output L03,
  output L10,
  output L11,
  output L12,
  output L13,
  output L20,
  output L21,
  output L22,
  output L23
);

  wire and_1_out, and_2_out, and_3_out, and_4_out, and_5_out, and_6_out, and_7_out, and_8_out, and_9_out,
       and_10_out, and_11_out, and_12_out, and_13_out, and_14_out, and_15_out, and_16_out, and_17_out,
       and_18_out, and_19_out, and_20_out, and_21_out, and_22_out, and_23_out, not_1_out, not_2_out,
       not_3_out, not_4_out, not_5_out, not_6_out, not_7_out, not_8_out, not_9_out, not_10_out, not_11_out,
       not_12_out, not_13_out, not_14_out, not_15_out, not_16_out, not_17_out, not_18_out, not_19_out,
       not_20_out, not_21_out, not_22_out, not_23_out, not_24_out, not_25_out;

  not not_1 (not_1_out, N1);
  not not_2 (not_2_out, N1);
  not not_3 (not_3_out, N0);
  not not_4 (not_4_out, N1);
  not not_5 (not_5_out, N0);
  not not_6 (not_6_out, N1);
  not not_7 (not_7_out, N2);
  not not_8 (not_8_out, N2);
  not not_9 (not_9_out, N0);
  not not_10 (not_10_out, N2);
  not not_11 (not_11_out, N1);
  not not_12 (not_12_out, N0);
  not not_13 (not_13_out, N2);
  not not_14 (not_14_out, N1);
  not not_15 (not_15_out, N0);
  not not_16 (not_16_out, N2);
  not not_17 (not_17_out, N1);
  not not_18 (not_18_out, N0);
  not not_19 (not_19_out, N1);
  not not_20 (not_20_out, N0);
  not not_21 (not_21_out, N1);
  not not_22 (not_22_out, N1);
  not not_23 (not_23_out, N0);
  not not_24 (not_24_out, N1);
  not not_25 (not_25_out, N0);
  or or_1 (L00, not_1_out, N0, N2);
  and and_1 (and_1_out, not_2_out, N0);
  and and_2 (and_2_out, N1, not_3_out);
  and and_3 (and_3_out, not_4_out, N0);
  and and_4 (and_4_out, N1, not_5_out);
  and and_5 (and_5_out, N2, not_6_out);
  and and_6 (and_6_out, not_7_out, N0);
  and and_7 (and_7_out, not_8_out, N1);
  and and_8 (and_8_out, N2, not_9_out);
  and and_9 (and_9_out, not_10_out, not_11_out, N0);
  and and_10 (and_10_out, N2, not_12_out);
  and and_11 (and_11_out, not_13_out, not_14_out, N0);
  and and_12 (and_12_out, N2, not_15_out);
  and and_13 (and_13_out, N2, N1);
  and and_14 (and_14_out, not_16_out, N0);
  and and_15 (and_15_out, N2, not_17_out);
  and and_16 (and_16_out, N2, not_18_out);
  and and_17 (and_17_out, not_19_out, N0);
  and and_18 (and_18_out, N1, not_20_out);
  and and_19 (and_19_out, N2, not_21_out);
  and and_20 (and_20_out, not_22_out, N0);
  and and_21 (and_21_out, N1, not_23_out);
  and and_22 (and_22_out, N2, not_24_out);
  and and_23 (and_23_out, N2, not_25_out);
  or or_2 (L01, and_1_out, and_2_out, N2);
  or or_3 (L02, and_3_out, and_4_out, and_5_out);
  or or_4 (L03, and_6_out, and_7_out, and_8_out);
  or or_5 (L11, and_9_out, and_10_out);
  or or_6 (L12, and_11_out, and_12_out, and_13_out);
  or or_7 (L13, and_14_out, and_15_out, and_16_out);
  or or_8 (L21, and_17_out, and_18_out, and_19_out);
  or or_9 (L22, and_20_out, and_21_out, and_22_out);
  or or_10 (L23, N1, and_23_out);

  assign L10 = 1'b1;
  assign L20 = 1'b1;
endmodule

module P1_3bit_20seg (
  input  N2,
  input  N1,
  input  N0,
  output L30,
  output L31,
  output L32,
  output L33,
  output L40,
  output L41,
  output L42,
  output L43
);

  wire and_2_out, and_3_out, and_4_out, and_5_out, and_6_out, not_1_out, not_2_out, not_3_out, not_4_out,
       not_5_out, not_6_out, not_7_out, not_8_out, not_9_out, not_10_out, not_11_out;

  not not_1 (not_1_out, N1);
  not not_2 (not_2_out, N0);
  not not_3 (not_3_out, N1);
  not not_4 (not_4_out, N2);
  not not_5 (not_5_out, N0);
  not not_6 (not_6_out, N0);
  not not_7 (not_7_out, N2);
  not not_8 (not_8_out, N0);
  not not_9 (not_9_out, N2);
  not not_10 (not_10_out, N0);
  or or_1 (L30, not_1_out, N0, N2);
  and and_1 (L31, N2, not_2_out);
  and and_2 (and_2_out, not_3_out, N0);
  and and_3 (and_3_out, not_4_out, N1);
  and and_4 (and_4_out, N2, not_5_out);
  or or_2 (L41, not_6_out, N1);
  or or_3 (L42, not_7_out, not_8_out);
  not not_11 (not_11_out, N1);
  and and_5 (and_5_out, not_9_out, N0);
  and and_6 (and_6_out, N2, not_10_out);
  or or_4 (L32, and_2_out, N2);
  or or_5 (L33, and_3_out, and_4_out);
  or or_6 (L43, not_11_out, and_5_out, and_6_out);

  assign L40 = 1'b1;
endmodule

module _3bit_to20seg (
  input  N2,
  input  N1,
  input  N0,
  output [3:0] Row0,
  output [3:0] Row1,
  output [3:0] Row2,
  output [3:0] Row3,
  output [3:0] Row4
);

  P2_3bit_20seg p2_3bit_20seg_1 (
    .N2(N2), .N1(N1), .N0(N0), .L00(Row0[3]), .L01(Row0[2]), .L02(Row0[1]), .L03(Row0[0]), .L10(Row1[3]),
    .L11(Row1[2]), .L12(Row1[1]), .L13(Row1[0]), .L20(Row2[3]), .L21(Row2[2]), .L22(Row2[1]), .L23(Row2[0]));
  P1_3bit_20seg p1_3bit_20seg_1 (
    .N2(N2), .N1(N1), .N0(N0), .L30(Row3[3]), .L31(Row3[2]), .L32(Row3[1]), .L33(Row3[0]), .L40(Row4[3]),
    .L41(Row4[2]), .L42(Row4[1]), .L43(Row4[0]));
endmodule

module LA2bit_to3bit (
  input  D1,
  input  D0,
  output N2,
  output N1,
  output N0
);

  wire and_1_out, and_2_out, not_1_out, not_2_out, not_3_out;

  not not_1 (not_1_out, D1);
  not not_2 (not_2_out, D0);
  not not_3 (not_3_out, D1);
  and and_1 (and_1_out, not_1_out, not_2_out);
  and and_2 (and_2_out, D1, D0);
  or or_1 (N0, not_3_out, D0);
  or or_2 (N2, and_1_out, and_2_out);

  assign N1 = 1'b1;
endmodule

module RA2bit_to3bit (
  input  D1,
  input  D0,
  output N2,
  output N1,
  output N0
);

  wire not_2_out;

  not not_1 (N2, D1);
  not not_2 (not_2_out, D1);
  or or_1 (N0, not_2_out, D0);

  assign N1 = 1'b1;
endmodule
